# Fritzing sketch ESPWebServer (saved by Fritzing 0.9.2b)
circuit board: 4.11486cm x 4.83972cm
breadboards: 1

parts:
  R2 = Resistor [tolerance=±5% resistance=10k package=THT]
  R3 = Resistor [tolerance=±5% resistance=10k package=THT]
  R4 = Resistor [tolerance=±5% resistance=330 package=THT]
  S1 = Pushbutton [part_number=RESET package="[THT]"]
  S3 = Pushbutton [part_number=FLASH package="[THT]"]
  U1 = ESP8266 WiFi Module [part_number=ESP8266]
  R5 = Resistor [tolerance=±5% resistance=10k package=THT]
  C1 = Electrolytic Capacitor [capacitance=1µF part_number=C1 package="100 mil [THT, electrolytic]"]
  R6 = Resistor [tolerance=±5% resistance=10k package=THT]
  S2 = Pushbutton [part_number=AP_MODE package="[THT]"]
  R1 = Resistor [tolerance=±5% resistance=10k part_number=R3 package=THT]
  Parte1 = DC-DC Power Module (3.3v)
  LED1 = LED - 5mm [color="Red (633nm)" package="5 mm [THT]"]

nets:
  GND: R2.Pin_0, S1.Pin_1, S1.Pin_2, S3.Pin_1, S3.Pin_2, U1.GND, R5.Pin_1, C1.-, Parte1.GND*
  N1: R2.Pin_1, U1.GPIO_4, S2.Pin_3, S2.Pin_4
  N2: R3.Pin_0, R4.Pin_0, U1.VCC, C1.+, R6.Pin_0, S2.Pin_1, S2.Pin_2, R1.Pin_0, Parte1.Vout
  N3: R3.Pin_1, S3.Pin_3, S3.Pin_4, U1.GPIO_0, LED1.cathode
  N4: R4.Pin_1, LED1.anode
  N5: S1.Pin_3, S1.Pin_4, U1.REST, R1.Pin_1
  N6: U1.CH_PD, R6.Pin_1
  N7: U1.GPIO_15, R5.Pin_0

custom parts:
  ESP8266 WiFi Module: Generic WiFi Module based on the ESP8266 with onboard PCB antenna and UART communications
  DC-DC Power Module (3.3v): DC-DC Power Module based con AMS1117-3.3 Input: DC 4.5~7V (input power must higher 1V than output power); Output: 3.3V (+/-0.05V error), 800mA
